// Logisim project simplification.circ as structural Verilog: 1 circuit, main circuit main
module main (
  input  x,
  input  z,
  input  y,
  output out_4
);

  wire and_1_out, not_1_out, or_1_out, or_2_out;

  or or_1 (or_1_out, x, z);
  or or_2 (or_2_out, z, y);
  and and_1 (and_1_out, or_1_out, y);
  not not_1 (not_1_out, or_2_out);
  or or_3 (out_4, and_1_out, not_1_out);

  // Notes on the sheet:
  //   Simplification
  //   (z + y)' + y(x + z)
endmodule
