// Logisim project zero-insertion-circuit.circ as structural Verilog: 1 circuit, main circuit main
module main (
  input  x,
  output z,
  output s
);

  wire and_1_out, and_2_out, and_3_out, and_4_out, and_6_out, and_7_out, and_8_out, and_9_out, and_10_out,
       and_11_out, clock_1_out, not_1_out, or_1_out, s_r_ff_1_q, s_r_ff_1_qn, s_r_ff_2_q, s_r_ff_2_qn,
       s_r_ff_3_q, s_r_ff_3_qn;

  not not_1 (not_1_out, x);
  and and_1 (and_1_out, x, s_r_ff_3_qn, s_r_ff_1_q);
  or or_1 (or_1_out, not_1_out, s_r_ff_1_q);
  and and_2 (and_2_out, s_r_ff_1_q, s_r_ff_2_q, x);
  and and_3 (and_3_out, s_r_ff_1_qn, x);
  or or_2 (z, and_3_out, and_4_out);
  and and_4 (and_4_out, s_r_ff_3_qn, x);
  and and_5 (s, x, s_r_ff_3_q, s_r_ff_1_q);
  and and_6 (and_6_out, s_r_ff_1_qn, x);
  and and_7 (and_7_out, 1'b1, s_r_ff_1_q);
  and and_8 (and_8_out, s_r_ff_2_qn, and_1_out);
  and and_9 (and_9_out, or_1_out, s_r_ff_2_q);
  and and_10 (and_10_out, s_r_ff_3_qn, and_2_out);
  and and_11 (and_11_out, or_1_out, s_r_ff_3_q);
  S_R_Flip_Flop s_r_ff_1 (
    .S(and_6_out), .clk(clock_1_out), .R(and_7_out), .Q(s_r_ff_1_q), .Qn(s_r_ff_1_qn));  // open: preset, reset, en
  S_R_Flip_Flop s_r_ff_2 (
    .S(and_8_out), .clk(clock_1_out), .R(and_9_out), .Q(s_r_ff_2_q), .Qn(s_r_ff_2_qn));  // open: preset, reset, en
  S_R_Flip_Flop s_r_ff_3 (
    .S(and_10_out), .clk(clock_1_out), .R(and_11_out), .Q(s_r_ff_3_q), .Qn(s_r_ff_3_qn));  // open: preset, reset, en
  Clock clock_1 (.out(clock_1_out));
endmodule
